# Fritzing sketch pico-wiring-05 (saved by Fritzing 0.9.3b)
breadboards: 1

parts:
  LED1 = smd LED [color="Red (633nm)" package="0603 [SMD]"]
  Mod1 = Raspberry Pi Pico
  S3 = Momentary Switch [package=ksa_sealed_tac_switch]
  R1 = Resistor [tolerance=±5% resistance=330 package=THT]
  LED2 = smd LED [color="Red (633nm)" package="0603 [SMD]"]
  R2 = Resistor [tolerance=±5% resistance=330 package=THT]
  LED3 = smd LED [color="Red (633nm)" package="0603 [SMD]"]
  R3 = Resistor [tolerance=±5% resistance=330 package=THT]
  Buzzer1 = Piezo Speaker

nets:
  N1: LED1.cathode, Mod1.pin_23, Mod1.pin_42, S3.3, LED2.cathode, LED3.cathode, Buzzer1.pin1
  N2: LED1.anode, R1.Pin_0
  N3: Mod1.pin_21, S3.2
  N4: Mod1.pin_22, R1.Pin_1
  N5: Mod1.pin_24, R2.Pin_1
  N6: Mod1.pin_25, R3.Pin_1
  N7: Mod1.pin_26, Buzzer1.pin2
  N8: LED2.anode, R2.Pin_0
  N9: LED3.anode, R3.Pin_0

notes:
  LED (GP17, pin22), LED (GP18, pin24), LED (GP19, pin24)
  Button (GP16, pin21)
  Buzzer (GP20, pin25)
  GND (pin23)

custom parts:
  Raspberry Pi Pico: Raspberry Pi Pico. Based around the RP2040 microcontroller the Pico is a low cost microcontroller device bringing Raspberry Pi quality, cost, and easy of use to the microcontroller space. Jan 2021, Split part in to two versions: tht (this one) and SMD. This one will drill holes for a .1 in header in pcb to allow plugging in the module as well as providing pads to solder the module to the top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
