# Fritzing sketch step-004 (saved by Fritzing 0.9.3b)
breadboards: 1

parts:
  LED1 = smd LED [color="Red (633nm)" package="0603 [SMD]"]
  R1 = Resistor [tolerance=±5% resistance=330 package=THT]
  Mod1 = Raspberry Pi Pico
  LED2 = smd LED [color="Red (633nm)" package="0603 [SMD]"]
  R2 = Resistor [tolerance=±5% resistance=330 package=THT]

nets:
  N1: LED1.cathode, Mod1.pin_3, Mod1.pin_42, LED2.cathode
  N2: LED1.anode, R1.Pin_0
  N3: R1.Pin_1, Mod1.pin_21
  N4: Mod1.pin_22, R2.Pin_1
  N5: LED2.anode, R2.Pin_0

notes:
  GPIO16 (pin21). GPIO17 (pin22)
  Gnd(pin 3)

custom parts:
  Raspberry Pi Pico: Raspberry Pi Pico. Based around the RP2040 microcontroller the Pico is a low cost microcontroller device bringing Raspberry Pi quality, cost, and easy of use to the microcontroller space. Jan 2021, Split part in to two versions: tht (this one) and SMD. This one will drill holes for a .1 in header in pcb to allow plugging in the module as well as providing pads to solder the module to the top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
