# Fritzing sketch step-001 (saved by Fritzing 0.9.3b)
breadboards: 1

parts:
  LED1 = smd LED [color="Red (633nm)" package="0603 [SMD]"]
  R1 = Resistor [tolerance=±5% resistance=330 package=THT]
  PiZero1 = Raspberry Pi Zero
  LED2 = smd LED [color="Red (633nm)" package="0603 [SMD]"]
  R2 = Resistor [tolerance=±5% resistance=330 package=THT]

nets:
  N1: LED1.cathode, PiZero1.GPIO19, LED2.cathode
  N2: LED1.anode, R1.Pin_0
  N3: R1.Pin_1, PiZero1.GPIO4_(GCLK)
  N4: PiZero1.Ground, R2.Pin_1
  N5: PiZero1.GPIO25_(GEN6), PiZero1.TV0
  N6: LED2.anode, R2.Pin_0

notes:
  GPIO17 (pin11), GPIO27(pin13)
  Gnd (pin6),
